# Fritzing sketch greenhouse (saved by Fritzing 0.9.3b)
breadboards: 1

parts:
  Mod1 = Raspberry Pi 4B  # not connected
  J1 = Raspberry Pi Header 40pin [package=THT]
  Part1 = Adafruit TSL2591 High Dynamic Range Digital Light Sensor [part_number="Adafruit #1980"]
  Part2 = BME280
  IC1 = MCP3008 8-channel 10-bit ADC [part_number=MCP3008]
  Part3 = Soil Moisture Sensor
  Part4 = Soil Moisture Sensor
  Part5 = Soil Moisture Sensor
  Part6 = Soil Moisture Sensor
  Part7 = Soil Moisture Sensor
  IC2 = Rasberry Pi NIOR Camera [chip_label=IC package="DIP (Dual Inline) [THT]"]  # not connected

nets:
  3V3: J1.3V3, Part1.VCC, Part2.VIN, IC1.no_name_yet#15, IC1.no_name_yet#16
  VCC: J1.5V, Part3.VCC, Part4.VCC, Part5.VCC, Part6.VCC, Part7.VCC
  N1: J1.GPIO2, Part1.SDA, Part2.SDA
  N2: J1.IO3, Part1.SCL, Part2.SCL
  GND: J1.GND, Part1.GND, Part2.GND, IC1.no_name_yet#9, IC1.no_name_yet#14, Part3.GND, Part4.GND, Part5.GND, Part6.GND, Part7.GND
  N3: J1.IO4, Part1.INT
  N4: J1.IO10, IC1.no_name_yet#11
  N5: J1.IO9, IC1.no_name_yet#12
  N6: J1.IO11, IC1.no_name_yet#13
  N7: J1.IO8, IC1.no_name_yet#10
  N8: IC1.no_name_yet#1, Part7.SIG
  N9: IC1.no_name_yet#2, Part6.SIG
  N10: IC1.no_name_yet#3, Part5.SIG
  N11: IC1.no_name_yet#4, Part4.SIG
  N12: IC1.no_name_yet#5, Part3.SIG

custom parts:
  Raspberry Pi Header 40pin: Raspberry Pi 40 pin header - for creating your own shields. (Mar 2020, bb: make breadboard friendly (.4in pin spacing) and add labels. Schematic add labels. PCB make oblong pins to allow routing traces between the pins.)
  Adafruit TSL2591 High Dynamic Range Digital Light Sensor: When the future is dazzlingly-bright, this ultra-high-range luminosity sensor will help you measure it. The TSL2591 luminosity sensor is an advanced digital light sensor, ideal for use in a wide range of light situations. Compared to low cost CdS cells, this sensor is more precise, allowing for exact lux calculations and can be configured for different gain/timing ranges to detect light ranges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
  Rasberry Pi NIOR Camera: Camera
